// Logisim project ALU.circ as structural Verilog: 1 circuit, main circuit main
module main (
  input  [15:0] in_1,
  input  in_2,
  input  [15:0] in_3,
  input  in_4,
  input  in_5,
  output [15:0] out_6,
  output ALU
);

  wire [15:0] multiplexer_1_out, not_1_out;

  assign not_1_out = ~in_3;  // NOT_Gate not_1, 16 bits wide
  Multiplexer #(.width(16)) multiplexer_1 (.in0(in_3), .in1(not_1_out), .out(multiplexer_1_out), .sel(in_4), .en(in_5));
  Adder #(.width(16)) adder_1 (.a(in_1), .b(multiplexer_1_out), .out(out_6), .cin(in_2), .cout(ALU));

  // Notes on the sheet:
  //   Load Inputs
endmodule
