// Logisim project Bus.circ as structural Verilog: 1 circuit, main circuit main
module main (
  input  [15:0] in_1,
  input  [2:0] in_2,
  input  [15:0] in_3,
  input  in_4,
  input  in_5,
  input  in_6,
  input  [2:0] in_7,
  input  Read_Bus,
  output [11:0] out_9,
  output [15:0] out_10,
  output [15:0] out_11,
  output [15:0] out_12
);

  wire decoder_1_out1, decoder_1_out2, decoder_1_out3, decoder_1_out4, decoder_1_out7;
  wire [11:0] adder_1_out, multiplexer_3_out, register_5_q;
  wire [15:0] bit_extender_1_out, bit_extender_2_out, multiplexer_1_out, register_4_q;

  Decoder #(.select(3)) decoder_1 (
    .out1(decoder_1_out1), .out2(decoder_1_out2), .out3(decoder_1_out3), .out4(decoder_1_out4),
    .out7(decoder_1_out7), .sel(in_2));  // open: out0, out5, out6, en
  Register #(.width(12)) register_1 (.D(in_1[11:0]), .en(decoder_1_out1), .Q(out_9), .clk(Read_Bus));  // open: clr
  Multiplexer #(.width(16)) multiplexer_1 (.in0(in_1), .in1(in_3), .out(multiplexer_1_out), .sel(in_4));  // open: en
  Register #(.width(16)) register_2 (.D(in_1), .en(decoder_1_out3), .Q(out_11), .clk(Read_Bus));  // open: clr
  assign bit_extender_1_out = {{4{1'b0}}, out_9};  // Bit_Extender bit_extender_1
  Register #(.width(16)) register_3 (
    .D(multiplexer_1_out), .en(decoder_1_out4), .Q(out_10), .clk(Read_Bus), .clr(in_6));
  Multiplexer #(.select(3), .width(16)) multiplexer_2 (
    .in1(bit_extender_1_out), .in2(bit_extender_2_out), .in3(out_11), .in4(out_10), .in7(register_4_q),
    .out(out_12), .sel(in_7));  // open: in0, in5, in6, en
  Multiplexer #(.width(12)) multiplexer_3 (
    .in0(adder_1_out), .in1(in_1[11:0]), .out(multiplexer_3_out), .sel(in_5));  // open: en
  Register #(.width(16)) register_4 (.D(in_1), .en(decoder_1_out7), .Q(register_4_q), .clk(Read_Bus));  // open: clr
  Register #(.width(12)) register_5 (
    .D(multiplexer_3_out), .en(decoder_1_out2), .Q(register_5_q), .clk(Read_Bus));  // open: clr
  Adder #(.width(12)) adder_1 (.a(register_5_q), .b({12{1'b0}}), .out(adder_1_out), .cin(1'b1));  // open: cout
  assign bit_extender_2_out = {{4{1'b0}}, register_5_q};  // Bit_Extender bit_extender_2

  // Notes on the sheet:
  //   MAR
  //   AC
  //   IR
  //   PC
  //   Write Bus
endmodule
