// Logisim project CU.circ as structural Verilog: 1 circuit, main circuit main
module main (
  input  [15:0] in_1,
  input  in_2,
  input  [15:0] in_3,
  output out_4,
  output out_5,
  output [2:0] out_6,
  output [2:0] out_7,
  output memory_read,
  output memory_write,
  output Inc_PC,
  output Clr_AC
);

  wire and_1_out, and_2_out, and_3_out, and_4_out, and_5_out, and_6_out, and_7_out, and_8_out, and_9_out,
       and_10_out, and_11_out, and_12_out, and_13_out, and_14_out, and_21_out, and_22_out, and_23_out,
       and_24_out, and_25_out, and_26_out, and_27_out, and_28_out, comparator_1_eq, comparator_1_gt,
       comparator_1_lt, not_1_out, not_2_out, not_3_out, not_4_out, not_5_out, not_6_out, not_7_out,
       or_7_out, or_8_out, or_9_out, or_10_out, or_11_out;
  wire [1:0] rom_1_data_2;
  wire [6:0] adder_1_out, multiplexer_1_out, multiplexer_2_out, register_1_q, register_2_q, rom_1_data;
  wire [14:9] rom_1_data_3;

  or or_1 (out_6[0], and_4_out, or_9_out, and_11_out);
  or or_2 (out_6[1], or_7_out, or_9_out, and_11_out);
  or or_3 (out_6[2], and_13_out, and_11_out);
  or or_4 (out_7[0], or_8_out, or_10_out, and_12_out);
  or or_5 (out_7[1], and_3_out, or_10_out, and_12_out);
  or or_6 (out_7[2], and_12_out, and_14_out);
  or or_7 (or_7_out, and_1_out, and_2_out);
  or or_8 (or_8_out, and_5_out, and_6_out);
  or or_9 (or_9_out, and_7_out, memory_write, and_8_out);
  or or_10 (or_10_out, and_9_out, memory_read, and_10_out);
  and and_1 (and_1_out, not_1_out, rom_1_data_3[13], not_2_out, not_4_out);
  and and_2 (and_2_out, rom_1_data_3[14], rom_1_data_3[13], not_2_out, rom_1_data_3[11]);
  and and_3 (and_3_out, rom_1_data_3[14], rom_1_data_3[13], not_2_out, not_4_out);
  and and_4 (and_4_out, rom_1_data_3[14], rom_1_data_3[13], not_2_out, not_4_out);
  and and_5 (and_5_out, not_1_out, rom_1_data_3[13], not_2_out, not_4_out);
  and and_6 (and_6_out, rom_1_data_3[14], not_3_out, not_2_out, not_4_out);
  and and_7 (and_7_out, not_1_out, not_3_out, not_2_out, rom_1_data_3[11]);
  and and_8 (and_8_out, rom_1_data_3[14], not_3_out, not_2_out, rom_1_data_3[11]);
  and and_9 (and_9_out, not_1_out, not_3_out, rom_1_data_3[12], not_4_out);
  and and_10 (and_10_out, rom_1_data_3[14], rom_1_data_3[13], not_2_out, rom_1_data_3[11]);
  and and_11 (and_11_out, rom_1_data_3[14], not_3_out, not_2_out, not_4_out);
  and and_12 (and_12_out, rom_1_data_3[14], not_3_out, not_2_out, rom_1_data_3[11]);
  and and_13 (and_13_out, not_1_out, not_3_out, rom_1_data_3[12], not_4_out);
  and and_14 (and_14_out, not_1_out, not_3_out, not_2_out, rom_1_data_3[11]);
  and and_15 (memory_read, not_1_out, rom_1_data_3[13], not_2_out, rom_1_data_3[11]);
  and and_16 (memory_write, rom_1_data_3[14], not_3_out, rom_1_data_3[12], not_4_out);
  and and_17 (Inc_PC, not_1_out, rom_1_data_3[13], rom_1_data_3[12], not_4_out);
  and and_18 (Clr_AC, rom_1_data_3[14], not_3_out, rom_1_data_3[12], rom_1_data_3[11]);
  not not_1 (not_1_out, rom_1_data_3[14]);
  not not_2 (not_2_out, rom_1_data_3[12]);
  not not_3 (not_3_out, rom_1_data_3[13]);
  not not_4 (not_4_out, rom_1_data_3[11]);
  ROM #(.addrWidth(7), .dataWidth(15)) rom_1 (
    .addr(register_1_q), .data({rom_1_data_3, rom_1_data_2, rom_1_data}));  // open: sel
  and and_19 (out_4, not_1_out, not_3_out, rom_1_data_3[12], rom_1_data_3[11]);
  and and_20 (out_5, not_1_out, rom_1_data_3[13], rom_1_data_3[12], rom_1_data_3[11]);
  Multiplexer #(.select(2), .width(7)) multiplexer_1 (
    .in0(rom_1_data), .in1(rom_1_data), .in2({1'b0, in_1[15:12], 2'b00}), .in3(register_2_q),
    .out(multiplexer_1_out), .sel(rom_1_data_2));  // open: en
  not not_5 (not_5_out, rom_1_data_3[9]);
  not not_6 (not_6_out, rom_1_data_3[10]);
  Adder #(.width(7)) adder_1 (.a(register_1_q), .b(7'b0000001), .out(adder_1_out));  // open: cin, cout
  and and_21 (and_21_out, not_6_out, not_5_out);
  and and_22 (and_22_out, not_6_out, rom_1_data_3[9]);
  and and_23 (and_23_out, rom_1_data_3[10], not_5_out);
  and and_24 (and_24_out, rom_1_data_3[10], rom_1_data_3[9]);
  Comparator #(.width(16)) comparator_1 (
    .a(in_3), .b({16{1'b0}}), .gt(comparator_1_gt), .eq(comparator_1_eq), .lt(comparator_1_lt));
  Register #(.width(7)) register_1 (.D(multiplexer_2_out), .Q(register_1_q), .clk(in_2));  // open: en, clr
  Multiplexer #(.width(7)) multiplexer_2 (
    .in0(adder_1_out), .in1(multiplexer_1_out), .out(multiplexer_2_out), .sel(or_11_out));  // open: en
  and and_25 (and_25_out, and_22_out, comparator_1_gt);
  and and_26 (and_26_out, and_23_out, comparator_1_eq);
  and and_27 (and_27_out, and_24_out, comparator_1_lt);
  Register #(.width(7)) register_2 (.D(register_1_q), .en(and_28_out), .Q(register_2_q), .clk(in_2));  // open: clr
  or or_11 (or_11_out, and_21_out, and_25_out, and_26_out, and_27_out);
  not not_7 (not_7_out, rom_1_data_2[0]);
  and and_28 (and_28_out, not_7_out, rom_1_data_2[1]);

  // Notes on the sheet:
  //   PC read
  //   PC write
  //   AR write
  //   MBR read
  //   MBR write
  //   AC read
  //   AR read
  //   IR read
  //   IR write
  //   AC write
  //   contents of rom_1 (hex, n*v repeats v):
  //   6801 5002 6003 3040 2805 2112 0 0 1009 5040 0 0 280d 1840 0 0 2811 3840 18*0 6025 0 0 0 5840 0 0 0
  //   c4 282e 1840 0 c4 6040 0 0 c4 2836 840 0 1039 c4 5040 5*0 2041 2842 3043 4848 2845 4846 4180 0 4100
  //   CAR
  //   SBR
endmodule
