// Logisim project Marie computer.circ as structural Verilog: 1 circuit, main circuit main
module main (
  output [15:0] out_1
);

  wire and_1_out, clock_1_out, main_1_clr_ac, main_1_inc_pc, main_1_memory_read, main_1_memory_write,
       main_1_out_4, main_1_out_5, not_1_out, xor_1_out;
  wire [2:0] main_1_out_6, main_1_out_7;
  wire [11:0] main_3_out_9;
  wire [15:0] main_2_out_6, main_3_out_10, main_3_out_11, main_3_out_12, multiplexer_1_out;

  CU_main main_1 (
    .in_1(out_1), .memory_read(main_1_memory_read), .memory_write(main_1_memory_write),
    .Inc_PC(main_1_inc_pc), .Clr_AC(main_1_clr_ac), .out_6(main_1_out_6), .out_7(main_1_out_7),
    .in_3(main_3_out_10), .out_4(main_1_out_4), .out_5(main_1_out_5), .in_2(clock_1_out));
  Clock clock_1 (.out(clock_1_out));
  xor xor_1 (xor_1_out, main_1_out_4, main_1_out_5);
  not not_1 (not_1_out, main_1_out_4);
  ALU_main main_2 (
    .in_1(main_3_out_10), .in_3(main_3_out_11), .out_6(main_2_out_6), .in_4(and_1_out), .in_5(xor_1_out));  // open: ALU, in_2
  and and_1 (and_1_out, not_1_out, main_1_out_5);
  RAM #(.addrWidth(12), .dataWidth(16), .bus("separate")) ram_1 (
    .addr(main_3_out_9), .din(main_3_out_12), .data(out_1), .str(main_1_memory_write), .ld(main_1_memory_read));  // open: sel, clk, clr
  Multiplexer #(.width(16)) multiplexer_1 (
    .in0(main_3_out_12), .in1(out_1), .out(multiplexer_1_out), .sel(main_1_memory_read));  // open: en
  Bus_main main_3 (
    .in_1(multiplexer_1_out), .in_2(main_1_out_7), .in_7(main_1_out_6), .out_12(main_3_out_12),
    .in_6(main_1_clr_ac), .in_5(main_1_inc_pc), .out_10(main_3_out_10), .out_9(main_3_out_9),
    .out_11(main_3_out_11), .in_3(main_2_out_6), .in_4(xor_1_out), .Read_Bus(clock_1_out));

  // Notes on the sheet:
  //   Main Memory
endmodule
